# Fritzing sketch B3_Blink (saved by Fritzing 0.8.5b)
breadboards: 1

parts:
  Part1 = Arduino Mega 2560 (Rev3)
  LED1 = LED - 5mm [color="Green (565nm)" package="5 mm [THT]"]
  R1 = Resistor [tolerance=±1% resistance=220 package=THT]

nets:
  N1: Part1.D13_PWM, LED1.anode
  N2: Part1.GND, R1.Pin_1
  N3: LED1.cathode, R1.Pin_0
