# Fritzing sketch B3_Bump (saved by Fritzing 0.8.5b)
breadboards: 1

parts:
  Part1 = Arduino Mega 2560 (Rev3)
  LED1 = LED - 5mm [color="Green (565nm)" package="5 mm [THT]"]
  R1 = Resistor [tolerance=±1% resistance=220 package=THT]
  S1 = SPST Switch [package=switch-spdt_kit]
  S2 = SPST Switch [package=switch-spdt_kit]

nets:
  N1: Part1.5V, LED1.anode
  N2: Part1.D46, S2.O
  N3: Part1.D47, S1.O
  N4: Part1.GND, R1.Pin_1, S1.P, S2.P
  N5: LED1.cathode, R1.Pin_0
