# Fritzing sketch B3_BumpBlinkLightSonic (saved by Fritzing 0.8.5b)
breadboards: 1

parts:
  Part1 = Arduino Mega 2560 (Rev3)
  LED1 = LED - 5mm [color="Green (565nm)" package="5 mm [THT]"]
  S1 = SPST Switch [package=switch-spdt_kit]
  S2 = SPST Switch [package=switch-spdt_kit]
  R1 = Resistor [tolerance=±1% resistance=330 package=THT]
  LED2 = LED - 5mm [color="Red (633nm)" package="5 mm [THT]"]
  R2 = Resistor [tolerance=±1% resistance=330 package=THT]
  R8 = Resistor [tolerance=±1% resistance=5.1k package=THT]
  R10 = PHOTOCELL [package=photocell-kit]
  R9 = Resistor [tolerance=±1% resistance=5.1k package=THT]
  R11 = PHOTOCELL [package=photocell-kit]
  Part3 = SRF05 Ultrasonic Rangefinder

nets:
  N1: Part1.A14, R8.Pin_1, R10.P$2
  N2: Part1.A15, R9.Pin_1, R11.P$1
  5V: Part1.5V, LED1.anode, LED2.anode, R10.P$1, R11.P$2, Part3.VCC
  N3: Part1.D46, S2.O, R1.Pin_0
  N4: Part1.D47, S1.O, R2.Pin_1
  N5: Part1.D50, Part3.Trig
  N6: Part1.D51, Part3.Echo
  GND: Part1.GND, S1.P, S2.P, R8.Pin_0, R9.Pin_0, Part3.GND
  N7: LED1.cathode, R1.Pin_1
  N8: LED2.cathode, R2.Pin_0
