# Fritzing sketch B3_Light (saved by Fritzing 0.8.5b)
breadboards: 1

parts:
  Part1 = Arduino Mega 2560 (Rev3)
  R4 = Resistor [tolerance=±1% resistance=5.1k package=THT]
  R5 = Resistor [tolerance=±1% resistance=5.1k package=THT]
  R6 = PHOTOCELL [package=photocell-kit]
  R7 = PHOTOCELL [package=photocell-kit]

nets:
  N1: Part1.A14, R5.Pin_1, R6.P$2
  N2: Part1.A15, R4.Pin_1, R7.P$1
  N3: Part1.5V, R6.P$1, R7.P$2
  N4: Part1.GND, R4.Pin_0, R5.Pin_0
