# Fritzing sketch B3_Sonic (saved by Fritzing 0.8.5b)
breadboards: 1

parts:
  Part1 = Arduino Mega 2560 (Rev3)
  Part2 = SRF05 Ultrasonic Rangefinder

nets:
  5V: Part1.5V, Part2.VCC
  N1: Part1.D50, Part2.Trig
  N2: Part1.D51, Part2.Echo
  GND: Part1.GND, Part2.GND
